# Fritzing sketch DigiSpark - Musica con Leds Navidad (saved by Fritzing 0.9.3b)

parts:
  Digispark1 = Digispark
  J2 = Piezo Speaker
  S1 = Momentary Switch [package=ksa_sealed_tac_switch]
  R1 = Resistor [tolerance=±5% resistance=100k package=THT]
  LED1 = LED - 3mm [color="Red (633nm)" package="3 mm [THT]"]
  LED2 = LED - 3mm [color="Green (565nm)" package="3 mm [THT]"]
  LED3 = LED - 3mm [color="Blue (525nm)" package="3 mm [THT]"]
  R2 = Resistor [tolerance=±5% resistance=220 package=THT]
  R3 = Resistor [tolerance=±5% resistance=220 package=THT]
  R4 = Resistor [tolerance=±5% resistance=220 package=THT]
  BAT3 = Battery Holders [package=battcom_20mm_pth]

nets:
  N1: Digispark1.VCC, S1.2
  N2: Digispark1.GND, J2.pin1, R1.Pin_1, BAT3.-
  N3: Digispark1.VIN, BAT3.+
  N4: Digispark1.P0, S1.4, R1.Pin_0
  N5: Digispark1.P1, J2.pin2
  N6: Digispark1.P2, LED3.anode
  N7: Digispark1.P3, LED2.anode
  N8: Digispark1.P4, LED1.anode
  N9: LED1.cathode, R2.Pin_1
  N10: LED2.cathode, R3.Pin_1
  N11: LED3.cathode, R4.Pin_1

custom parts:
  Digispark: The Digispark is an Attiny85 based microcontroller development board similar to the Arduino line, only cheaper, smaller, and a bit less powerful. With a whole host of shields to extend its functionality and the ability to use the familiar Arduino IDE the Digispark is a great way to jump into electronics, or perfect for when an Arduino is too big or too much.
